# Fritzing sketch CIRC01 (saved by Fritzing 0.9.2b)
circuit board: 2.01896cm x 1.5389cm
breadboards: 1

parts:
  LED = LEDs [package=led10mm]
  resistor = Resistor [tolerance=±5% resistance=560 package=THT]
  Part1 = Arduino Uno (Rev3)
  V1 = DC Power [voltage=5]

nets:
  N1: LED.C, resistor.Pin_0
  pin 13: LED.A, Part1.D13/SCK
  GND: resistor.Pin_1, Part1.GND, V1.V-
  5V: Part1.5V, V1.V+

notes:
  (green-blue-brown)
  Arduino
  (light emitting diode)
  (ground) (-)
  longer lead
  anode
  cathode
