# Fritzing sketch CIRC02 (saved by Fritzing 0.9.2b)
circuit board: 6.43099cm x 1.66082cm
breadboards: 1

parts:
  R1 = Resistor [tolerance=±5% resistance=560 package=THT]
  R7 = Resistor [tolerance=±5% resistance=560 package=THT]
  R6 = Resistor [tolerance=±5% resistance=560 package=THT]
  R5 = Resistor [tolerance=±5% resistance=560 package=THT]
  R4 = Resistor [tolerance=±5% resistance=560 package=THT]
  R3 = Resistor [tolerance=±5% resistance=560 package=THT]
  R2 = Resistor [tolerance=±5% resistance=560 package=THT]
  LED1 = LED - 5mm [color="Red (633nm)" package="5 mm [THT]"]
  LED8 = LED - 5mm [color="Red (633nm)" package="5 mm [THT]"]
  LED7 = LED - 5mm [color="Red (633nm)" package="5 mm [THT]"]
  LED6 = LED - 5mm [color="Red (633nm)" package="5 mm [THT]"]
  LED5 = LED - 5mm [color="Red (633nm)" package="5 mm [THT]"]
  LED4 = LED - 5mm [color="Red (633nm)" package="5 mm [THT]"]
  LED3 = LED - 5mm [color="Red (633nm)" package="5 mm [THT]"]
  LED2 = LED - 5mm [color="Red (633nm)" package="5 mm [THT]"]
  R8 = Resistor [tolerance=±5% resistance=560 package=THT]
  Part1 = Arduino Uno (Rev3)

nets:
  GND: R1.Pin_0, R7.Pin_0, R6.Pin_0, R5.Pin_0, R4.Pin_0, R3.Pin_0, R2.Pin_0, R8.Pin_0, Part1.GND
  N1: R1.Pin_1, LED1.cathode
  N2: R7.Pin_1, LED7.cathode
  N3: R6.Pin_1, LED6.cathode
  N4: R5.Pin_1, LED5.cathode
  N5: R4.Pin_1, LED4.cathode
  N6: R3.Pin_1, LED3.cathode
  N7: R2.Pin_1, LED2.cathode
  pin 2: LED1.anode, Part1.D2
  N8: LED8.cathode, R8.Pin_1
  pin 9: LED8.anode, Part1.D9_PWM
  pin 8: LED7.anode, Part1.D8
  pin 7: LED6.anode, Part1.D7
  pin 6: LED5.anode, Part1.D6_PWM
  pin 5: LED4.anode, Part1.D5_PWM
  pin 4: LED3.anode, Part1.D4
  pin 3: LED2.anode, Part1.D3_PWM
  5V: Part1.5V

notes:
  longer
  lead
